// Logisim project ashishpractcal1.circ as structural Verilog: 1 circuit, main circuit main
module main (
  input  in_1,
  input  in_2,
  input  in_3,
  input  in_4,
  output out_5,
  output out_6,
  output out_7,
  output out_8
);

  xor xor_1 (out_6, in_1, in_2);
  xor xor_2 (out_7, in_2, in_3);
  xor xor_3 (out_8, in_3, in_4);

  assign out_5 = in_1;

  // Notes on the sheet:
  //   Binary to Grey code conversion by Ashish Mangal 2000270130036
endmodule
